# Fritzing sketch 1. Alternate Blink fzz chart (saved by Fritzing 0.9.3b)
breadboards: 1

parts:
  Raspberry_Pi_1 = Raspberry Pi 3 [part_number=RPI-3-V1.2]
  R1 = PHOTOCELL [package=photocell-kit]
  R4 = Resistor [tolerance=±5% resistance=220 package="2512 [SMD]"]
  LED1 = smd LED [color="Red (633nm)" package="1206 [SMD]"]
  R3 = PHOTOCELL [package=photocell]

nets:
  3V3: Raspberry_Pi_1.3v3, Raspberry_Pi_1.3V3, R1.P$1, LED1.anode, R3.P$1
  N1: Raspberry_Pi_1.GPIO2, Raspberry_Pi_1.GPIO3, Raspberry_Pi_1.GND, R1.P$2, R4.Pin_1, R3.P$2
  N2: R4.Pin_0, LED1.cathode
