# Fritzing sketch 2. Clock Seconds fzz chart (saved by Fritzing 0.9.3b)
breadboards: 1

parts:
  Raspberry_Pi_1 = Raspberry Pi 3 [part_number=RPI-3-V1.2]
  R4 = Resistor [tolerance=±5% resistance=220 package="2512 [SMD]"]
  LED22 = smd LED [color="Red (633nm)" package="1206 [SMD]"]
  LED23 = smd LED [color="Red (633nm)" package="1206 [SMD]"]
  LED24 = smd LED [color="Red (633nm)" package="1206 [SMD]"]
  LED25 = smd LED [color="Red (633nm)" package="1206 [SMD]"]
  LED26 = smd LED [color="Red (633nm)" package="1206 [SMD]"]
  LED27 = smd LED [color="Red (633nm)" package="1206 [SMD]"]
  LED28 = smd LED [color="Red (633nm)" package="1206 [SMD]"]
  LED29 = smd LED [color="Red (633nm)" package="1206 [SMD]"]
  LED30 = smd LED [color="Red (633nm)" package="1206 [SMD]"]
  LED31 = smd LED [color="Red (633nm)" package="1206 [SMD]"]
  LED32 = smd LED [color="Red (633nm)" package="1206 [SMD]"]
  LED33 = smd LED [color="Red (633nm)" package="1206 [SMD]"]
  LED34 = smd LED [color="Red (633nm)" package="1206 [SMD]"]
  LED35 = smd LED [color="Red (633nm)" package="1206 [SMD]"]
  LED36 = smd LED [color="Red (633nm)" package="1206 [SMD]"]

nets:
  N1: Raspberry_Pi_1.GPIO2, LED24.anode
  N2: Raspberry_Pi_1.GPIO3, LED22.anode
  N3: Raspberry_Pi_1.GIPO4, LED23.anode
  N4: Raspberry_Pi_1.GIPO17, LED30.anode
  N5: Raspberry_Pi_1.GIPO27, LED28.anode
  N6: Raspberry_Pi_1.GIPO22, LED29.anode
  N7: Raspberry_Pi_1.GIPO10, LED33.anode
  N8: Raspberry_Pi_1.GIPO9, LED31.anode
  N9: Raspberry_Pi_1.GIPO11, LED32.anode
  N10: Raspberry_Pi_1.GIPO13, LED36.anode
  N11: Raspberry_Pi_1.GIPO19, LED34.anode
  N12: Raspberry_Pi_1.GIPO26, LED35.anode
  N13: Raspberry_Pi_1.GND, R4.Pin_1
  N14: Raspberry_Pi_1.GIPO18, LED26.anode
  N15: Raspberry_Pi_1.GIPO15, LED25.anode
  N16: Raspberry_Pi_1.GIPO14, LED27.anode
  N17: R4.Pin_0, LED22.cathode, LED23.cathode, LED24.cathode, LED25.cathode, LED26.cathode, LED27.cathode, LED28.cathode, LED29.cathode, LED30.cathode, LED31.cathode, LED32.cathode, LED33.cathode, LED34.cathode, LED35.cathode, LED36.cathode
