# Fritzing sketch 2. Clock fzz chart (saved by Fritzing 0.9.3b)
breadboards: 1

parts:
  Raspberry_Pi_1 = Raspberry Pi 3 [part_number=RPI-3-V1.2]
  LED1 = smd LED [color="Red (633nm)" package="1206 [SMD]"]
  R4 = Resistor [tolerance=±5% resistance=220 package="2512 [SMD]"]
  U1 = M40 [package=1x40_offset]
  LED2 = smd LED [color="Red (633nm)" package="1206 [SMD]"]
  LED3 = smd LED [color="Red (633nm)" package="1206 [SMD]"]
  LED10 = smd LED [color="Red (633nm)" package="1206 [SMD]"]
  LED11 = smd LED [color="Red (633nm)" package="1206 [SMD]"]
  LED12 = smd LED [color="Red (633nm)" package="1206 [SMD]"]
  LED13 = smd LED [color="Red (633nm)" package="1206 [SMD]"]
  LED14 = smd LED [color="Red (633nm)" package="1206 [SMD]"]
  LED15 = smd LED [color="Red (633nm)" package="1206 [SMD]"]
  LED16 = smd LED [color="Red (633nm)" package="1206 [SMD]"]
  LED17 = smd LED [color="Red (633nm)" package="1206 [SMD]"]
  LED18 = smd LED [color="Red (633nm)" package="1206 [SMD]"]

nets:
  N1: Raspberry_Pi_1.GPIO2, LED1.anode
  N2: Raspberry_Pi_1.GPIO3, LED2.anode
  N3: Raspberry_Pi_1.GPIO4, LED3.anode
  N4: Raspberry_Pi_1.GPIO17, LED18.anode
  N5: Raspberry_Pi_1.GPIO27, LED17.anode
  N6: Raspberry_Pi_1.GPIO22, LED16.anode
  N7: Raspberry_Pi_1.GPIO10, LED10.anode
  N8: Raspberry_Pi_1.GPIO9, LED11.anode
  N9: Raspberry_Pi_1.GPIO11, LED12.anode
  N10: Raspberry_Pi_1.GND, R4.Pin_0
  N11: Raspberry_Pi_1.GPIO18, LED13.anode
  N12: Raspberry_Pi_1.GPIO15, LED15.anode
  N13: Raspberry_Pi_1.GPIO14, LED14.anode
  N14: R4.Pin_1, U1.1
  N15: U1.4, LED3.cathode
  N16: U1.7, LED13.cathode
  N17: U1.10, LED16.cathode
  N18: U1.13, LED12.cathode
