# Fritzing sketch 3. LED Turn on based on Light Intensity (saved by Fritzing 0.9.3b)
breadboards: 1

parts:
  Raspberry_Pi_1 = Raspberry Pi 3 [part_number=RPI-3-V1.2]
  R3 = Photocell (LDR) [package=THT]
  LED1 = smd LED [color="Red (633nm)" package="0603 [SMD]"]
  C1 = Capacitor Polarized [package=panasonic_c]

nets:
  N1: Raspberry_Pi_1.3v3, R3.pin_1
  N2: Raspberry_Pi_1.GPIO2, LED1.cathode
  N3: Raspberry_Pi_1.GPIO3, R3.pin_0, C1.+
  N4: Raspberry_Pi_1.GND, LED1.anode, C1.-
